// Digital circuit ALU8bits.dig as structural Verilog
module ALU8bits (
  input  C,
  input  Sub,
  input  Inv,
  input  [7:0] A,
  input  [7:0] B,
  output [7:0] Sai,
  output Vf0,
  output C_out,
  output VfN
);

  wire alubasic_1_c_out, alubasic_2_c_out, alubasic_3_c_out, alubasic_4_c_out, alubasic_5_c_out,
       alubasic_6_c_out, alubasic_7_c_out, or_1_out, xor_1_out;

  or or_1 (or_1_out, C, Sub);
  ALUbasic alubasic_1 (
    .C_in(or_1_out), .Inverter(Inv), .A(A[0]), .B(B[0]), .Sub(Sub), .\Saída (Sai[0]), .C_out(alubasic_1_c_out));
  Seven_Seg_Hex seven_seg_hex_1 (.d(Sai[7:4]), .dp(1'b0));
  Seven_Seg_Hex seven_seg_hex_2 (.d(Sai[3:0]), .dp(1'b0));
  ALUbasic alubasic_2 (
    .C_in(alubasic_1_c_out), .Inverter(Inv), .A(A[1]), .B(B[1]), .Sub(Sub), .\Saída (Sai[1]),
    .C_out(alubasic_2_c_out));
  ALUbasic alubasic_3 (
    .C_in(alubasic_2_c_out), .Inverter(Inv), .A(A[2]), .B(B[2]), .Sub(Sub), .\Saída (Sai[2]),
    .C_out(alubasic_3_c_out));
  nor nor_1 (Vf0, Sai[4], Sai[5], Sai[6], Sai[7], Sai[0], Sai[1], Sai[2], Sai[3]);
  ALUbasic alubasic_4 (
    .C_in(alubasic_3_c_out), .Inverter(Inv), .A(A[3]), .B(B[3]), .Sub(Sub), .\Saída (Sai[3]),
    .C_out(alubasic_4_c_out));
  Seven_Seg_Hex seven_seg_hex_3 (.d(A[7:4]), .dp(1'b0));
  Seven_Seg_Hex seven_seg_hex_4 (.d(A[3:0]), .dp(1'b0));
  ALUbasic alubasic_5 (
    .C_in(alubasic_4_c_out), .Inverter(Inv), .A(A[4]), .B(B[4]), .Sub(Sub), .\Saída (Sai[4]),
    .C_out(alubasic_5_c_out));
  ALUbasic alubasic_6 (
    .C_in(alubasic_5_c_out), .Inverter(Inv), .A(A[5]), .B(B[5]), .Sub(Sub), .\Saída (Sai[5]),
    .C_out(alubasic_6_c_out));
  ALUbasic alubasic_7 (
    .C_in(alubasic_6_c_out), .Inverter(Inv), .A(A[6]), .B(B[6]), .Sub(Sub), .\Saída (Sai[6]),
    .C_out(alubasic_7_c_out));
  Seven_Seg_Hex seven_seg_hex_5 (.d(B[7:4]), .dp(1'b0));
  Seven_Seg_Hex seven_seg_hex_6 (.d(B[3:0]), .dp(1'b0));
  ALUbasic alubasic_8 (
    .C_in(alubasic_7_c_out), .Inverter(Inv), .A(A[7]), .B(B[7]), .Sub(Sub), .\Saída (Sai[7]), .C_out(C_out));
  xor xor_1 (xor_1_out, Sub, C_out);
  and and_1 (VfN, Sub, xor_1_out);

  // Other names for the same wires on the sheet: RegA[7:0] = A; RegB[7:0] = B
endmodule
