// Digital circuit ALUbasic.dig as structural Verilog
module ALUbasic (
  input  C_in,
  input  Inverter,
  input  A,
  input  B,
  input  Sub,
  output \Saída ,
  output C_out
);

  wire and_1_out, and_2_out, and_3_out, and_4_out, not_1_out, xor_1_out, xor_2_out, xor_3_out;

  xor xor_1 (xor_1_out, Sub, B);
  xor xor_2 (xor_2_out, A, not_1_out);
  not not_1 (not_1_out, Inverter);
  and and_1 (and_1_out, Inverter, C_in);
  and and_2 (and_2_out, xor_1_out, Inverter);
  and and_3 (and_3_out, xor_2_out, and_2_out);
  xor xor_3 (xor_3_out, and_2_out, xor_2_out);
  or or_1 (C_out, and_3_out, and_4_out);
  and and_4 (and_4_out, and_1_out, xor_3_out);
  xor xor_4 (\Saída , xor_3_out, and_1_out);
endmodule
