// Digital circuit Buffer8bits.dig as structural Verilog
module Buffer8bits (
  input  [7:0] Entrada,
  input  Hab,
  output [7:0] \Saída 
);

  assign \Saída [0] = Hab ? Entrada[0] : 1'bz;  // Driver driver_1
  assign \Saída [1] = Hab ? Entrada[1] : 1'bz;  // Driver driver_2
  assign \Saída [2] = Hab ? Entrada[2] : 1'bz;  // Driver driver_3
  assign \Saída [3] = Hab ? Entrada[3] : 1'bz;  // Driver driver_4
  assign \Saída [4] = Hab ? Entrada[4] : 1'bz;  // Driver driver_5
  assign \Saída [5] = Hab ? Entrada[5] : 1'bz;  // Driver driver_6
  assign \Saída [6] = Hab ? Entrada[6] : 1'bz;  // Driver driver_7
  assign \Saída [7] = Hab ? Entrada[7] : 1'bz;  // Driver driver_8
endmodule
