// Digital circuit Contador.dig as structural Verilog
module Contador (
  input  Clear,
  input  CLK,
  input  Habilitar,
  output S1,
  output S2
);

  flipflopJK flipflopjk_1 (.J(Clear), .K(Clear), .CLK(CLK), .Preset(Clear), .Clear(Habilitar), .Q(S1));  // open: Q_2
  flipflopJK flipflopjk_2 (.J(Clear), .K(Clear), .CLK(S1), .Preset(Clear), .Clear(Habilitar), .Q(S2));  // open: Q_2
endmodule
