// Digital circuit Contador5bits.dig as structural Verilog
module Contador5bits (
  input  [7:0] Entrada_pc,
  input  Carregar,
  input  Hab_Cont,
  input  CLK,
  input  Clear,
  input  \Hab_Saída ,
  output [5:0] \Saída_pc 
);

  wire and_1_out, and_2_out, and_3_out, and_4_out, and_5_out, and_6_out, and_7_out, and_8_out, and_9_out,
       and_10_out, and_11_out, and_12_out, and_13_out, and_14_out, and_15_out, and_16_out, and_17_out,
       not_1_out, not_2_out, not_3_out, not_4_out, not_5_out, not_6_out, or_1_out, or_2_out, or_3_out,
       or_4_out, or_5_out, or_6_out;
  wire [2:0] pulldown_1_out;
  wire [5:0] B0_out;

  Seven_Seg_Hex seven_seg_hex_1 (.d({2'b00, B0_out[5:4]}), .dp(CLK));
  Seven_Seg_Hex seven_seg_hex_2 (.d(B0_out[3:0]), .dp(CLK));
  or or_1 (or_1_out, Clear, and_1_out);
  or or_2 (or_2_out, Clear, and_2_out);
  or or_3 (or_3_out, Clear, and_3_out);
  or or_4 (or_4_out, Clear, and_4_out);
  or or_5 (or_5_out, Clear, and_5_out);
  or or_6 (or_6_out, Clear, and_6_out);
  and and_1 (and_1_out, not_1_out, Carregar);
  and and_2 (and_2_out, not_2_out, Carregar);
  and and_3 (and_3_out, not_3_out, Carregar);
  and and_4 (and_4_out, not_4_out, Carregar);
  and and_5 (and_5_out, not_5_out, Carregar);
  and and_6 (and_6_out, not_6_out, Carregar);
  not not_1 (not_1_out, and_7_out);
  not not_2 (not_2_out, and_8_out);
  not not_3 (not_3_out, and_9_out);
  not not_4 (not_4_out, and_10_out);
  not not_5 (not_5_out, and_11_out);
  not not_6 (not_6_out, and_12_out);
  and and_7 (and_7_out, Carregar, Entrada_pc[0]);
  and and_8 (and_8_out, Carregar, Entrada_pc[1]);
  and and_9 (and_9_out, Carregar, Entrada_pc[2]);
  and and_10 (and_10_out, Carregar, Entrada_pc[3]);
  and and_11 (and_11_out, Carregar, Entrada_pc[4]);
  and and_12 (and_12_out, Carregar, Entrada_pc[5]);
  JK_FF_AS jk_ff_as_1 (
    .Set(and_7_out), .J(Hab_Cont), .C(CLK), .K(Hab_Cont), .Clr(or_1_out), .Q(B0_out[0]));  // open: nQ
  JK_FF_AS jk_ff_as_2 (
    .Set(and_8_out), .J(and_13_out), .C(CLK), .K(and_13_out), .Clr(or_2_out), .Q(B0_out[1]));  // open: nQ
  JK_FF_AS jk_ff_as_3 (
    .Set(and_9_out), .J(and_14_out), .C(CLK), .K(and_14_out), .Clr(or_3_out), .Q(B0_out[2]));  // open: nQ
  JK_FF_AS jk_ff_as_4 (
    .Set(and_10_out), .J(and_15_out), .C(CLK), .K(and_15_out), .Clr(or_4_out), .Q(B0_out[3]));  // open: nQ
  JK_FF_AS jk_ff_as_5 (
    .Set(and_11_out), .J(and_16_out), .C(CLK), .K(and_16_out), .Clr(or_5_out), .Q(B0_out[4]));  // open: nQ
  JK_FF_AS jk_ff_as_6 (
    .Set(and_12_out), .J(and_17_out), .C(CLK), .K(and_17_out), .Clr(or_6_out), .Q(B0_out[5]));  // open: nQ
  and and_13 (and_13_out, Hab_Cont, B0_out[0]);
  and and_14 (and_14_out, Hab_Cont, and_13_out, B0_out[1]);
  and and_15 (and_15_out, Hab_Cont, and_14_out, B0_out[2]);
  and and_16 (and_16_out, Hab_Cont, and_15_out, B0_out[3]);
  and and_17 (and_17_out, Hab_Cont, and_16_out, B0_out[4]);
  assign \Saída_pc [0] = \Hab_Saída  ? B0_out[0] : 1'bz;  // Driver driver_1
  assign \Saída_pc [1] = \Hab_Saída  ? B0_out[1] : 1'bz;  // Driver driver_2
  assign \Saída_pc [2] = \Hab_Saída  ? B0_out[2] : 1'bz;  // Driver driver_3
  assign \Saída_pc [3] = \Hab_Saída  ? B0_out[3] : 1'bz;  // Driver driver_4
  assign \Saída_pc [4] = \Hab_Saída  ? B0_out[4] : 1'bz;  // Driver driver_5
  assign \Saída_pc [5] = \Hab_Saída  ? B0_out[5] : 1'bz;  // Driver driver_6
  PullDown #(.Bits(3)) pulldown_1 (.out(pulldown_1_out));
endmodule
