// Digital circuit SEMAFORO 09-10.dig as structural Verilog
module SEMAFORO_09_10 (
  input  A
);

  wire A_t, and_1_out, and_2_out, and_3_out, and_4_out, and_5_out, B, C, D, G, not_1_out, not_2_out,
       or_1_out, or_2_out, or_3_out, S1, S2, T;
  wire [3:0] counter_1_out, undriven;

  and and_1 (and_1_out, T, G);
  and and_2 (and_2_out, T, A_t);
  or or_1 (or_1_out, and_1_out, and_2_out);
  Counter counter_1 (.en(1'b1), .C(A), .clr(1'b0), .out(counter_1_out[0]));  // open: ovf
  or or_2 (or_2_out, S1, S2);
  and and_3 (and_3_out, C, or_2_out);
  and and_4 (and_4_out, C, D, not_1_out);
  not not_1 (not_1_out, B);
  and and_5 (and_5_out, B, C, not_2_out);
  not not_2 (not_2_out, A_t);
  or or_3 (or_3_out, and_4_out, and_5_out);
  // Pins of 1 and 8 bits meet at {undriven, counter_1_out}
endmodule
