// Digital circuit aula 09-10 1.dig as structural Verilog
module aula_09_10_1 (
);

  wire A, and_1_out, and_2_out, G, T;

  and and_1 (and_1_out, G, A);
  and and_2 (and_2_out, T, and_1_out);
endmodule
