// Digital circuit basicD_FF.dig as structural Verilog
module basicD_FF (
  input  D,
  input  CLK,
  input  OE,
  output Q,
  output nQ
);

  wire nand_1_out, nand_2_out, or_1_out, or_2_out;

  nand nand_1 (nand_1_out, CLK, D);
  nand nand_2 (nand_2_out, nand_1_out, CLK);
  or or_1 (or_1_out, ~nand_1_out, ~or_2_out);  // Or
  or or_2 (or_2_out, ~or_1_out, ~nand_2_out);  // Or
  assign Q = OE ? or_1_out : 1'bz;  // Driver driver_1
  assign nQ = OE ? or_2_out : 1'bz;  // Driver driver_2

  // Notes on the sheet:
  //   OE: default 1
endmodule

/* Test case TesteD:
OE CLK  D   Q ~Q 
0   X   X   X  X  
1   0   X   X  X
1   1   X   X  X
1   C   X   X  X
1   C   0   0  1
1   C   1   1  0
*/
