// Digital circuit fullD_FF.dig as structural Verilog
module fullD_FF (
  input  nPR,
  input  D,
  input  nCLR,
  input  CLK,
  input  nLe,
  input  OE,
  output Q,
  output nQ
);

  wire and_1_out, and_2_out, nand_1_out, nand_2_out, nand_3_out, nand_4_out, not_1_out, or_1_out, or_2_out,
       or_3_out;

  not not_1 (not_1_out, nLe);
  and and_1 (and_1_out, or_2_out, nLe);
  and and_2 (and_2_out, not_1_out, D);
  or or_1 (or_1_out, and_1_out, and_2_out);
  nand nand_1 (nand_1_out, nPR, nand_4_out, nand_2_out);
  nand nand_2 (nand_2_out, nand_1_out, CLK, nCLR);
  nand nand_3 (nand_3_out, nand_2_out, CLK, nand_4_out);
  nand nand_4 (nand_4_out, nand_3_out, or_1_out, nCLR);
  or or_2 (or_2_out, ~nPR, ~nand_2_out, ~or_3_out);  // Or
  or or_3 (or_3_out, ~or_2_out, ~nand_3_out, ~nCLR);  // Or
  assign Q = OE ? or_2_out : 1'bz;  // Driver driver_1
  assign nQ = OE ? or_3_out : 1'bz;  // Driver driver_2

  // Notes on the sheet:
  //   nPR: default 1
  //   nCLR: default 1
  //   OE: default 1
endmodule

/* Test case TesteD:
~PR ~CLR CLK D   Q ~Q
0   0   X   X   X  X
0   1   X   X   1  0
1   0   X   X   0  1
1   1   0   X   X  X
1   1   1   X   X  X
1   1   C   X   X  X
1   1   C   0   0  1
1   1   C   1   1  0
*/
