// Digital circuit msJK_ff.dig as structural Verilog
module msJK_ff (
  input  K,
  input  CLK,
  input  OE,
  input  J,
  output Q,
  output nQ
);

  wire nand_1_out, nand_2_out, nand_3_out, nand_4_out, nand_5_out, nand_6_out, nand_7_out, nand_8_out,
       not_1_out;

  nand nand_1 (nand_1_out, CLK, K, nand_7_out);
  nand nand_2 (nand_2_out, nand_8_out, J, CLK);
  nand nand_3 (nand_3_out, nand_2_out, nand_4_out);
  nand nand_4 (nand_4_out, nand_3_out, nand_1_out);
  not not_1 (not_1_out, CLK);
  nand nand_5 (nand_5_out, nand_3_out, not_1_out);
  nand nand_6 (nand_6_out, not_1_out, nand_4_out);
  nand nand_7 (nand_7_out, nand_5_out, nand_8_out);
  nand nand_8 (nand_8_out, nand_7_out, nand_6_out);
  assign Q = OE ? nand_7_out : 1'bz;  // Driver driver_1
  assign nQ = OE ? nand_8_out : 1'bz;  // Driver driver_2

  // Notes on the sheet:
  //   OE: default 1
endmodule

/* Test case TesteD:
OE CLK  J  K   Q ~Q 
0   X   X  X   X  X  
1   0   X  X   X  X
1   1   X  X   X  X
1   C   0  0   X  X
1   C   0  0   X  X
1   C   1  0   1  0
1   C   0  1   0  1
1   C   1  1   1  0
1   C   1  1   0  1
1   C   1  1   1  0
1   C   1  1   0  1
*/
