// Digital circuit 1.dig as structural Verilog
module _1 (
  input  J,
  input  K
);

  wire and_1_out, and_2_out, nand_1_out, nand_2_out, nand_3_out, nand_4_out, undriven;

  nand nand_1 (nand_1_out, J, nand_4_out, nand_2_out);
  nand nand_2 (nand_2_out, nand_1_out, nand_3_out, K);
  and and_1 (and_1_out, nand_1_out, undriven);
  and and_2 (and_2_out, undriven, nand_2_out);
  nand nand_3 (nand_3_out, and_1_out, nand_4_out);
  nand nand_4 (nand_4_out, nand_3_out, and_2_out);
  LED led_1 (.in(nand_3_out));
  LED led_2 (.in(nand_4_out));
endmodule
