// Digital circuit Regis_Principal.dig as structural Verilog
module Regis_Principal (
  input  [7:0] Data_in,
  input  \Hab_Saída ,
  input  Hab,
  output [7:0] Hab_out
);

  flipflopD flipflopd_1 (.Dados(Data_in[7]), .Habiltiar(Hab), .\Hab_Saída (\Hab_Saída ), .\Saída (Hab_out[7]));
  flipflopD flipflopd_2 (.Dados(Data_in[6]), .Habiltiar(Hab), .\Hab_Saída (\Hab_Saída ), .\Saída (Hab_out[6]));
  flipflopD flipflopd_3 (.Dados(Data_in[5]), .Habiltiar(Hab), .\Hab_Saída (\Hab_Saída ), .\Saída (Hab_out[5]));
  flipflopD flipflopd_4 (.Dados(Data_in[4]), .Habiltiar(Hab), .\Hab_Saída (\Hab_Saída ), .\Saída (Hab_out[4]));
  flipflopD flipflopd_5 (.Dados(Data_in[3]), .Habiltiar(Hab), .\Hab_Saída (\Hab_Saída ), .\Saída (Hab_out[3]));
  flipflopD flipflopd_6 (.Dados(Data_in[2]), .Habiltiar(Hab), .\Hab_Saída (\Hab_Saída ), .\Saída (Hab_out[2]));
  flipflopD flipflopd_7 (.Dados(Data_in[1]), .Habiltiar(Hab), .\Hab_Saída (\Hab_Saída ), .\Saída (Hab_out[1]));
  flipflopD flipflopd_8 (.Dados(Data_in[0]), .Habiltiar(Hab), .\Hab_Saída (\Hab_Saída ), .\Saída (Hab_out[0]));
endmodule
