// Digital circuit Registrador_8Bits.dig as structural Verilog
module Registrador_8Bits (
  input  Hab_E,
  input  _0,
  input  _1,
  input  _2,
  input  _3,
  input  Hab_S,
  input  _4,
  input  _5,
  input  _6,
  input  _7,
  output _0_2,
  output _1_2,
  output _2_2,
  output _3_2,
  output _4_2,
  output _5_2,
  output _6_2,
  output _7_2
);

  wire nand_1_out, nand_2_out, nand_3_out, nand_4_out, nand_5_out, nand_6_out, nand_7_out, nand_8_out,
       nand_9_out, nand_10_out, nand_11_out, nand_12_out, nand_13_out, nand_14_out, nand_15_out, nand_16_out,
       nand_17_out, nand_18_out, nand_19_out, nand_20_out, nand_21_out, nand_22_out, nand_23_out,
       nand_24_out, nand_25_out, nand_26_out, nand_27_out, nand_28_out, nand_29_out, nand_30_out,
       nand_31_out, nand_32_out, not_1_out, not_2_out, not_3_out, not_4_out, not_5_out, not_6_out, not_7_out,
       not_8_out;

  nand nand_1 (nand_1_out, _4, Hab_E);
  nand nand_2 (nand_2_out, Hab_E, _0);
  nand nand_3 (nand_3_out, nand_7_out, nand_1_out);
  nand nand_4 (nand_4_out, nand_2_out, nand_8_out);
  not not_1 (not_1_out, _4);
  nand nand_5 (nand_5_out, not_1_out, Hab_E);
  nand nand_6 (nand_6_out, Hab_E, not_2_out);
  not not_2 (not_2_out, _0);
  assign _4_2 = Hab_S ? nand_3_out : 1'bz;  // Driver driver_1
  nand nand_7 (nand_7_out, nand_3_out, nand_5_out);
  nand nand_8 (nand_8_out, nand_6_out, nand_4_out);
  assign _0_2 = Hab_S ? nand_4_out : 1'bz;  // Driver driver_2
  nand nand_9 (nand_9_out, _5, Hab_E);
  nand nand_10 (nand_10_out, Hab_E, _1);
  nand nand_11 (nand_11_out, nand_15_out, nand_9_out);
  not not_3 (not_3_out, _5);
  not not_4 (not_4_out, _1);
  nand nand_12 (nand_12_out, nand_10_out, nand_18_out);
  assign _5_2 = Hab_S ? nand_11_out : 1'bz;  // Driver driver_3
  nand nand_13 (nand_13_out, not_3_out, Hab_E);
  nand nand_14 (nand_14_out, Hab_E, not_4_out);
  assign _1_2 = Hab_S ? nand_12_out : 1'bz;  // Driver driver_4
  nand nand_15 (nand_15_out, nand_11_out, nand_13_out);
  nand nand_16 (nand_16_out, _6, Hab_E);
  nand nand_17 (nand_17_out, Hab_E, _2);
  nand nand_18 (nand_18_out, nand_14_out, nand_12_out);
  nand nand_19 (nand_19_out, nand_23_out, nand_16_out);
  nand nand_20 (nand_20_out, nand_17_out, nand_24_out);
  not not_5 (not_5_out, _6);
  nand nand_21 (nand_21_out, not_5_out, Hab_E);
  nand nand_22 (nand_22_out, Hab_E, not_6_out);
  not not_6 (not_6_out, _2);
  assign _6_2 = Hab_S ? nand_19_out : 1'bz;  // Driver driver_5
  nand nand_23 (nand_23_out, nand_19_out, nand_21_out);
  nand nand_24 (nand_24_out, nand_22_out, nand_20_out);
  assign _2_2 = Hab_S ? nand_20_out : 1'bz;  // Driver driver_6
  nand nand_25 (nand_25_out, _7, Hab_E);
  nand nand_26 (nand_26_out, Hab_E, _3);
  nand nand_27 (nand_27_out, nand_31_out, nand_25_out);
  not not_7 (not_7_out, _7);
  not not_8 (not_8_out, _3);
  nand nand_28 (nand_28_out, nand_26_out, nand_32_out);
  assign _7_2 = Hab_S ? nand_27_out : 1'bz;  // Driver driver_7
  nand nand_29 (nand_29_out, not_7_out, Hab_E);
  nand nand_30 (nand_30_out, Hab_E, not_8_out);
  assign _3_2 = Hab_S ? nand_28_out : 1'bz;  // Driver driver_8
  nand nand_31 (nand_31_out, nand_27_out, nand_29_out);
  nand nand_32 (nand_32_out, nand_30_out, nand_28_out);
endmodule
