// Digital circuit flipflopD.dig as structural Verilog
module flipflopD (
  input  Dados,
  input  Habiltiar,
  input  \Hab_Saída ,
  output \Saída 
);

  wire nand_1_out, nand_2_out, nand_3_out, nand_4_out, not_1_out;

  not not_1 (not_1_out, Dados);
  nand nand_1 (nand_1_out, Dados, Habiltiar);
  nand nand_2 (nand_2_out, not_1_out, Habiltiar);
  nand nand_3 (nand_3_out, nand_1_out, nand_4_out);
  nand nand_4 (nand_4_out, nand_2_out, nand_3_out);
  assign \Saída  = \Hab_Saída  ? nand_3_out : 1'bz;  // Driver driver_1
endmodule
