// Digital circuit flipflopD_AS.dig as structural Verilog
module flipflopD_AS (
  input  Entrada,
  input  CLK,
  input  Set,
  input  Clear,
  output Q,
  output nQ
);

  wire nand_1_out, nand_2_out, not_1_out;

  not not_1 (not_1_out, Entrada);
  nand nand_1 (nand_1_out, Entrada, CLK);
  nand nand_2 (nand_2_out, CLK, not_1_out);
  nand nand_3 (Q, Set, nand_1_out, nQ);
  nand nand_4 (nQ, Q, nand_2_out, Clear);
endmodule
