// Digital circuit flipflopJK.dig as structural Verilog
module flipflopJK (
  input  J,
  input  K,
  input  CLK,
  input  Preset,
  input  Clear,
  output Q,
  output Q_2
);

  wire nand_1_out, nand_2_out, nand_3_out, nand_4_out, nand_5_out, nand_6_out, not_1_out;

  nand nand_1 (nand_1_out, CLK, J, Q_2);
  nand nand_2 (nand_2_out, CLK, K, Q);
  nand nand_3 (nand_3_out, nand_2_out, Clear, nand_4_out);
  not not_1 (not_1_out, CLK);
  nand nand_4 (nand_4_out, nand_1_out, Preset, nand_3_out);
  nand nand_5 (nand_5_out, nand_4_out, not_1_out);
  nand nand_6 (nand_6_out, nand_3_out, not_1_out);
  nand nand_7 (Q, nand_5_out, Preset, Q_2);
  nand nand_8 (Q_2, nand_6_out, Clear, Q);
endmodule
