// Digital circuit sap1.dig as structural Verilog
module sap1 (
  input  Base_Clk
);

  wire ACC_e, ALU_CYin, ALU_INV, ALU_OUTe, ALU_RSLTe, ALU_SUB, and_5_out, and_6_out, and_7_out,
       decoder_1_out_0, decoder_1_out_1, DIRECTAddr_e, FNeg, FZero, HabADDRIO, HabADDRRAM, HabIO, HabIO1s,
       HabIO1x, HabIO_RD, HabIO_WR, HabRAM, HabRAM_RD, HabRAM_WR, HabWR_RD, JNeg, Jump, JZero, Lpc,
       not_1_out, NXT_I, or_2_out, PCCNT_e, PCOUT_e, RESET_out, RInst_E, RST, SW1_out, SW2_out, SW3_out,
       SW4_out;
  wire [2:0] counter_1_out;
  wire [3:0] regis_principal_1_hab_out, regis_principal_1_hab_out_2, regis_principal_5_hab_out;
  wire [5:0] pulldown_1_out;
  wire [7:0] ALU_dsp, driver_1_out, multiplexer_2_out, regis_principal_3_hab_out, regis_principal_4_hab_out;
  wire [7:2] regis_principal_2_hab_out;
  wire [7:4] regis_principal_5_hab_out_2;
  wire [11:0] rom_1_d;

  DipSwitch SW1 (.out(SW1_out));
  and and_1 (HabRAM_RD, HabRAM, not_1_out);
  and and_2 (HabRAM_WR, not_1_out, HabRAM);
  and and_3 (HabIO_WR, HabIO, not_1_out);
  and and_4 (HabIO_RD, not_1_out, HabIO);
  Multiplexer multiplexer_1 (.sel(decoder_1_out_0), .in_0(SW2_out), .in_1(SW1_out), .out(multiplexer_2_out[0]));
  and and_5 (and_5_out, HabIO_RD, HabIO1x);
  not not_1 (not_1_out, HabWR_RD);
  DipSwitch SW2 (.out(SW2_out));
  Decoder decoder_1 (.sel(HabIO1s), .out_0(decoder_1_out_0), .out_1(decoder_1_out_1));
  PullDown #(.Bits(6)) pulldown_1 (.out(pulldown_1_out));
  assign driver_1_out = and_5_out ? {multiplexer_2_out[7], pulldown_1_out, multiplexer_2_out[0]} : 8'bz;  // Driver driver_1
  DipSwitch SW3 (.out(SW3_out));
  or or_1 (Lpc, and_6_out, Jump, and_7_out);
  and and_6 (and_6_out, FNeg, JNeg);
  and and_7 (and_7_out, FZero, JZero);
  DipSwitch SW4 (.out(SW4_out));
  Multiplexer multiplexer_2 (.sel(decoder_1_out_1), .in_0(SW4_out), .in_1(SW3_out), .out(multiplexer_2_out[7]));
  RAMDualPort #(.AddrBits(8), .Bits(8)) ramdualport_1 (
    .A({regis_principal_1_hab_out_2, regis_principal_1_hab_out}), .Din(driver_1_out), .str(HabRAM),
    .C(Base_Clk), .ld(HabRAM_RD), .D(driver_1_out));
  Regis_Principal regis_principal_1 (
    .Data_in(driver_1_out), .\Hab_Saída (1'b1), .Hab(HabADDRRAM),
    .Hab_out({regis_principal_1_hab_out_2, regis_principal_1_hab_out}));
  PullUp #(.Bits(8)) pullup_1 (.out(driver_1_out));
  Seven_Seg_Hex seven_seg_hex_1 (.d(regis_principal_1_hab_out_2), .dp(1'b0));
  or or_2 (or_2_out, RST, NXT_I);
  Counter #(.Bits(3)) counter_1 (.en(1'b1), .C(Base_Clk), .clr(or_2_out), .out(counter_1_out));  // open: ovf
  Regis_Principal regis_principal_2 (
    .Data_in(driver_1_out), .\Hab_Saída (1'b1), .Hab(HabADDRIO),
    .Hab_out({regis_principal_2_hab_out, HabIO1x, HabIO1s}));
  Seven_Seg_Hex seven_seg_hex_2 (.d(regis_principal_1_hab_out), .dp(1'b0));
  Seven_Seg_Hex seven_seg_hex_3 (.d(rom_1_d[3:0]), .dp(1'b0));
  Seven_Seg_Hex seven_seg_hex_4 (.d({1'b0, counter_1_out}), .dp(1'b0));
  LookUpTable #(.Bits(19)) lookuptable_1 (
    .in0(counter_1_out[0]), .in1(counter_1_out[1]), .in2(counter_1_out[2]), .in3(rom_1_d[0]),
    .in4(rom_1_d[1]), .in5(rom_1_d[2]), .in6(rom_1_d[3]),
    .out({HabADDRIO, JNeg, JZero, HabWR_RD, ALU_CYin, ALU_INV, ALU_SUB, HabIO, HabRAM, ALU_OUTe, ALU_RSLTe, ACC_e, HabADDRRAM, DIRECTAddr_e, RInst_E, NXT_I, PCOUT_e, PCCNT_e, Jump}));
  Seven_Seg_Hex seven_seg_hex_5 (.d(regis_principal_2_hab_out[7:4]), .dp(1'b0));
  assign driver_1_out = DIRECTAddr_e ? rom_1_d[11:4] : 8'bz;  // Driver driver_2
  Seven_Seg_Hex seven_seg_hex_6 (.d({regis_principal_2_hab_out[3:2], HabIO1x, HabIO1s}), .dp(1'b0));
  LED led_1 (.in(ALU_RSLTe));
  Regis_Principal regis_principal_3 (
    .Data_in(driver_1_out), .\Hab_Saída (1'b1), .Hab(ALU_RSLTe), .Hab_out(regis_principal_3_hab_out));
  ROM #(.AddrBits(6), .Bits(12)) rom_1 (
    .A({regis_principal_5_hab_out_2[5:4], regis_principal_5_hab_out}), .sel(1'b1), .D(rom_1_d));
  Seven_Seg_Hex seven_seg_hex_7 (.d({2'b00, regis_principal_5_hab_out_2[5:4]}), .dp(1'b0));
  Seven_Seg_Hex seven_seg_hex_8 (.d(regis_principal_4_hab_out[7:4]), .dp(1'b0));
  Regis_Principal regis_principal_4 (
    .Data_in(driver_1_out), .\Hab_Saída (1'b1), .Hab(ACC_e), .Hab_out(regis_principal_4_hab_out));
  LED led_2 (.in(ALU_OUTe));
  Regis_Principal regis_principal_5 (
    .Data_in(driver_1_out), .\Hab_Saída (1'b1), .Hab(RInst_E),
    .Hab_out({regis_principal_5_hab_out_2, regis_principal_5_hab_out}));
  Seven_Seg_Hex seven_seg_hex_9 (.d(regis_principal_5_hab_out), .dp(1'b0));
  Seven_Seg_Hex seven_seg_hex_10 (.d(regis_principal_4_hab_out[3:0]), .dp(1'b0));
  assign driver_1_out = ALU_OUTe ? ALU_dsp : 8'bz;  // Driver driver_3
  ALU8bits alu8bits_1 (
    .C(ALU_CYin), .Sub(ALU_SUB), .Inv(ALU_INV), .A(regis_principal_4_hab_out), .B(regis_principal_3_hab_out),
    .Sai(ALU_dsp), .Vf0(FZero), .VfN(FNeg));  // open: C_out
  LED led_3 (.in(PCOUT_e));
  Seven_Seg_Hex seven_seg_hex_11 (.d(ALU_dsp[7:4]), .dp(1'b0));
  Contador5bits contador5bits_1 (
    .Entrada_pc(driver_1_out), .Carregar(Lpc), .Hab_Cont(PCCNT_e), .CLK(Base_Clk), .Clear(RST),
    .\Hab_Saída (PCOUT_e), .\Saída_pc (driver_1_out[5:0]));
  Seven_Seg_Hex seven_seg_hex_12 (.d(ALU_dsp[3:0]), .dp(1'b0));
  // NotConnected on driver_1_out[7:6]
  D_FF_AS d_ff_as_1 (.Set(RESET_out), .D(1'b0), .C(Base_Clk), .Clr(1'b0), .Q(RST));  // open: nQ
  Button RESET (.out(RESET_out));

  // Other names for the same wires on the sheet: CLK = Base_Clk

  // Notes on the sheet:
  //   Base_Clk: Hz: 3
  //   contents of lookuptable_1 (hex, n*v repeats v):
  //   2014,2002,2008,5*0,2014,2060,2,2008,4*0,2014,a420,2002,2008,4*0
  //   ,2014,20a0,2002,2008,4*0,2014,2060,2480,2,2008,0,0,0,2014,2060
  //   ,2500,2,2008,0,0,0,2014,2060,3500,2,2008,0,0,0,2014,2060,a600
  //   ,2002,2008,0,0,0,2014,21,2008,5*0,2014,2,12020,2008,4*0,2014,2
  //   ,22020,2008,4*0,2014,2002,2008,5*0,2014,42020,ac02,2008,4*0,2014
  //   ,42020,2c02,2008,4*0,2014,2002,2008,5*0,2014,2008
  //   contents of rom_1 (hex, n*v repeats v):
  //   121,302,301,302,451,122,303,125,27,23,601,20c,604,6,99,305,37
  //   ,326,99,455,307,20c,98
endmodule
